# Fritzing sketch InputStage_Vol_Tone 03 (saved by Fritzing 0.8.7b)
circuit board: 13.6869cm x 5.75091cm
breadboards: 1

parts:
  HousingConnect1 = female pin header, 10 pins [form="♀ (female)"]
  4660 = IC, DIP package, 14 pins [chip_label=CD4660]
  4660_2 = IC, DIP package, 14 pins [chip_label=CD4660]
  4660_3 = IC, DIP package, 14 pins [chip_label=CD4660]
  4660_4 = IC, DIP package, 14 pins [chip_label=CD4660]
  InverterOutput = female pin header, 4 pins [form="♀ (female)"]
  Controls = female pin header, 4 pins [form="♀ (female)"]
  outputXs = female pin header, 4 pins [form="♀ (female)"]
  power = female pin header, 2 pins [form="♀ (female)"]

nets:
  N1: HousingConnect1.pin7, 4660_3.pin9, 4660_3.pin10
  N2: HousingConnect1.pin8, 4660_3.pin2, 4660_3.pin3
  N3: HousingConnect1.pin9, 4660_4.pin9, 4660_4.pin10
  N4: HousingConnect1.pin10, 4660_4.pin2, 4660_4.pin3
  N5: 4660.pin2, 4660.pin3
  N6: 4660.pin4, 4660.pin11, InverterOutput.pin1
  N7: 4660.pin5, 4660.pin6
  N8: 4660.pin7, 4660_2.pin7, 4660_3.pin7, 4660_4.pin7, power.pin1
  N9: 4660.pin8, outputXs.pin1
  N10: 4660.pin9, 4660.pin10
  N11: 4660.pin12, 4660.pin13
  N12: 4660_2.pin2, 4660_2.pin3
  N13: 4660_2.pin4, 4660_2.pin11, InverterOutput.pin2
  N14: 4660_2.pin5, 4660_2.pin6
  N15: 4660_2.pin8, outputXs.pin2
  N16: 4660_2.pin9, 4660_2.pin10
  N17: 4660_2.pin12, 4660_2.pin13
  N18: 4660_2.pin14, 4660_3.pin14, 4660_4.pin14, power.pin2
  N19: 4660_3.pin1, 4660_3.pin8, outputXs.pin3
  N20: 4660_3.pin4, 4660_3.pin11, InverterOutput.pin3
  N21: 4660_3.pin5, 4660_3.pin6, Controls.pin3
  N22: 4660_3.pin12, 4660_3.pin13, Controls.pin4
  N23: 4660_4.pin1, 4660_4.pin8, outputXs.pin4
  N24: 4660_4.pin4, 4660_4.pin11, InverterOutput.pin4
  N25: 4660_4.pin5, 4660_4.pin6, Controls.pin1
  N26: 4660_4.pin12, 4660_4.pin13, Controls.pin2

notes:
  A1
  B1
  Y1
  X1
  +V
  -V
  X2
  A2
  B2
