# Fritzing sketch SPDT Inverter-VT-PCB (saved by Fritzing 0.9.0b)
circuit board: 8.05906cm x 2.06274cm
breadboards: 1

parts:
  Controls = female pin header, 13 pins [form="♀ (female)"]
  Vin = female pin header, 3 pins [form="♀ (female)"]
  Str = female pin header, 3 pins [form="♀ (female)"]
  Inv = female pin header, 3 pins [form="♀ (female)"]
  V100 = female pin header, 3 pins [form="♀ (female)"]
  V80 = female pin header, 3 pins [form="♀ (female)"]
  V60 = female pin header, 3 pins [form="♀ (female)"]
  V40 = female pin header, 3 pins [form="♀ (female)"]
  V20 = female pin header, 3 pins [form="♀ (female)"]
  V0 = female pin header, 3 pins [form="♀ (female)"]
  T200 = female pin header, 3 pins [form="♀ (female)"]
  T100 = female pin header, 3 pins [form="♀ (female)"]
  T50 = female pin header, 3 pins [form="♀ (female)"]
  T25 = female pin header, 3 pins [form="♀ (female)"]
  Ton/off = female pin header, 3 pins [form="♀ (female)"]

nets:
  N1: Controls.pin1, Str.pin2
  N2: Controls.pin2, Inv.pin2
  N3: Controls.pin3, V100.pin2
  N4: Controls.pin4, V80.pin2
  N5: Controls.pin5, V60.pin2
  N6: Controls.pin6, V40.pin2
  N7: Controls.pin7, V20.pin2
  N8: Controls.pin8, V0.pin2
  N9: Controls.pin9, T200.pin2
  N10: Controls.pin10, T100.pin2
  N11: Controls.pin11, T50.pin2
  N12: Controls.pin12, T25.pin2
  N13: Controls.pin13, Ton/off.pin2
  N14: Vin.pin1, Str.pin1, Inv.pin1, V100.pin1, V80.pin1, V60.pin1, V40.pin1, V20.pin1, V0.pin1, T200.pin1, T100.pin1, T50.pin1, T25.pin1, Ton/off.pin1
  N15: Vin.pin3, Str.pin3, Inv.pin3, V100.pin3, V80.pin3, V60.pin3, V40.pin3, V20.pin3, V0.pin3, T200.pin3, T100.pin3, T50.pin3, T25.pin3, Ton/off.pin3

notes:
  V+
  V-
  n/a
