# Fritzing sketch SPDT Switch-Array-PCB (saved by Fritzing 0.9.0b)
circuit board: 6.38526cm x 11.9258cm
breadboards: 1

parts:
  C+ = female pin header, 5 pins [form="♀ (female)"]
  B- = female pin header, 5 pins [form="♀ (female)"]
  B+ = female pin header, 5 pins [form="♀ (female)"]
  C- = female pin header, 5 pins [form="♀ (female)"]
  D+ = female pin header, 5 pins [form="♀ (female)"]
  D- = female pin header, 5 pins [form="♀ (female)"]
  Out+ = female pin header, 5 pins [form="♀ (female)"]
  Out- = female pin header, 5 pins [form="♀ (female)"]
  D-_2 = female pin header, 5 pins [form="♀ (female)"]
  D+_2 = female pin header, 5 pins [form="♀ (female)"]
  C-_2 = female pin header, 5 pins [form="♀ (female)"]
  B+_2 = female pin header, 5 pins [form="♀ (female)"]
  B-_2 = female pin header, 5 pins [form="♀ (female)"]
  C+_2 = female pin header, 5 pins [form="♀ (female)"]
  Out-_2 = female pin header, 5 pins [form="♀ (female)"]
  Out+_2 = female pin header, 5 pins [form="♀ (female)"]
  D-_3 = female pin header, 5 pins [form="♀ (female)"]
  D-_4 = female pin header, 5 pins [form="♀ (female)"]
  D+_3 = female pin header, 5 pins [form="♀ (female)"]
  D+_4 = female pin header, 5 pins [form="♀ (female)"]
  C-_3 = female pin header, 5 pins [form="♀ (female)"]
  C-_4 = female pin header, 5 pins [form="♀ (female)"]
  C+_3 = female pin header, 5 pins [form="♀ (female)"]
  C+_4 = female pin header, 5 pins [form="♀ (female)"]
  Out-_3 = female pin header, 5 pins [form="♀ (female)"]
  Out+_3 = female pin header, 5 pins [form="♀ (female)"]
  D-_5 = female pin header, 5 pins [form="♀ (female)"]
  D-_6 = female pin header, 5 pins [form="♀ (female)"]
  D+_5 = female pin header, 5 pins [form="♀ (female)"]
  D+_6 = female pin header, 5 pins [form="♀ (female)"]
  Out-_4 = female pin header, 5 pins [form="♀ (female)"]
  Out+_4 = female pin header, 5 pins [form="♀ (female)"]
  A+ = female pin header, 7 pins [form="♀ (female)"]
  D-_7 = female pin header, 1 pin [form="♀ (female)"]
  D+_7 = female pin header, 1 pin [form="♀ (female)"]
  Vin = female pin header, 2 pins [form="♀ (female)"]
  C-_5 = female pin header, 3 pins [form="♀ (female)"]
  C+_5 = female pin header, 3 pins [form="♀ (female)"]
  B-_3 = female pin header, 5 pins [form="♀ (female)"]
  B+_3 = female pin header, 5 pins [form="♀ (female)"]
  A- = female pin header, 7 pins [form="♀ (female)"]

nets:
  N1: C+.pin2, B-.pin2, B+.pin2, C-.pin2, D+.pin2, D-.pin2, Out+.pin2, Out-.pin2, D-_2.pin2, D+_2.pin2, C-_2.pin2, B+_2.pin2, B-_2.pin2, C+_2.pin2, Out-_2.pin2, Out+_2.pin2, D-_3.pin2, D-_4.pin2, D+_3.pin2, D+_4.pin2, C-_3.pin2, C-_4.pin2, C+_3.pin2, C+_4.pin2, Out-_3.pin2, Out+_3.pin2, D-_5.pin2, D-_6.pin2, D+_5.pin2, D+_6.pin2, Out-_4.pin2, Out+_4.pin2, Vin.pin1
  N2: C+.pin3, A+.pin3
  N3: C+.pin4, B-.pin4, B+.pin4, C-.pin4, D+.pin4, D-.pin4, Out+.pin4, Out-.pin4, D-_2.pin4, D+_2.pin4, C-_2.pin4, B+_2.pin4, B-_2.pin4, C+_2.pin4, Out-_2.pin4, Out+_2.pin4, D-_3.pin4, D-_4.pin4, D+_3.pin4, D+_4.pin4, C-_3.pin4, C-_4.pin4, C+_3.pin4, C+_4.pin4, Out-_3.pin4, Out+_3.pin4, D-_5.pin4, D-_6.pin4, D+_5.pin4, D+_6.pin4, Out-_4.pin4, Out+_4.pin4, Vin.pin2
  N4: B-.pin3, A+.pin2
  N5: B+.pin3, A+.pin1
  N6: C-.pin3, A+.pin4
  N7: D+.pin3, A+.pin5
  N8: D-.pin3, A+.pin6
  N9: Out+.pin3, A+.pin7
  N10: Out-.pin3, A-.pin7
  N11: D-_2.pin3, A-.pin6
  N12: D+_2.pin3, A-.pin5
  N13: C-_2.pin3, A-.pin4
  N14: B+_2.pin3, A-.pin1
  N15: B-_2.pin3, A-.pin2
  N16: C+_2.pin3, A-.pin3
  N17: Out-_2.pin3, B-_3.pin5
  N18: Out+_2.pin3, B+_3.pin5
  N19: D-_3.pin3, B+_3.pin4
  N20: D-_4.pin3, B-_3.pin4
  N21: D+_3.pin3, B+_3.pin3
  N22: D+_4.pin3, B-_3.pin3
  N23: C-_3.pin3, B+_3.pin2
  N24: C-_4.pin3, B-_3.pin2
  N25: C+_3.pin3, B+_3.pin1
  N26: C+_4.pin3, B-_3.pin1
  N27: Out-_3.pin3, C-_5.pin3
  N28: Out+_3.pin3, C+_5.pin3
  N29: D-_5.pin3, C-_5.pin2
  N30: D-_6.pin3, C+_5.pin2
  N31: D+_5.pin3, C+_5.pin1
  N32: D+_6.pin3, C-_5.pin1
  N33: Out-_4.pin3, D-_7.pin1
  N34: Out+_4.pin3, D+_7.pin1

notes:
  V+
  B+
  B-
  C+
  C-
  D+
  D-
  Out+
  Out-
  V-
