# Fritzing sketch SPDT-JUMPER-Switch-Array-PCB-big-pads (saved by Fritzing 0.9.1b)
circuit board: 7.20605cm x 14.4947cm
breadboards: 1

parts:
  Out+ = female pin header, 3 pins [form="♀ (female)"]
  A- = female pin header, 7 pins [form="♀ (female)"]
  B+ = female pin header, 5 pins [form="♀ (female)"]
  B- = female pin header, 5 pins [form="♀ (female)"]
  C+ = female pin header, 3 pins [form="♀ (female)"]
  C- = female pin header, 3 pins [form="♀ (female)"]
  D+ = female pin header, 1 pin [form="♀ (female)"]
  D- = female pin header, 1 pin [form="♀ (female)"]
  Vin = female pin header, 2 pins [form="♀ (female)"]
  D-_2 = female pin header, 4 pins [form="♀ (female)"]
  D+_2 = female pin header, 4 pins [form="♀ (female)"]
  C-_2 = female pin header, 4 pins [form="♀ (female)"]
  C+_2 = female pin header, 4 pins [form="♀ (female)"]
  B-_2 = female pin header, 4 pins [form="♀ (female)"]
  B+_2 = female pin header, 4 pins [form="♀ (female)"]
  A+ = female pin header, 7 pins [form="♀ (female)"]
  B+1 = female pin header, 4 pins [form="♀ (female)"]
  B-1 = female pin header, 4 pins [form="♀ (female)"]
  C+1 = female pin header, 4 pins [form="♀ (female)"]
  C-1 = female pin header, 4 pins [form="♀ (female)"]
  D-1 = female pin header, 4 pins [form="♀ (female)"]
  Out- = female pin header, 3 pins [form="♀ (female)"]
  D+1 = female pin header, 4 pins [form="♀ (female)"]
  C+2 = female pin header, 4 pins [form="♀ (female)"]
  C-2 = female pin header, 4 pins [form="♀ (female)"]
  D+2 = female pin header, 4 pins [form="♀ (female)"]
  D-2 = female pin header, 4 pins [form="♀ (female)"]
  Out+_2 = female pin header, 3 pins [form="♀ (female)"]
  Out-_2 = female pin header, 3 pins [form="♀ (female)"]
  D-3 = female pin header, 4 pins [form="♀ (female)"]
  D+3 = female pin header, 4 pins [form="♀ (female)"]
  C-3 = female pin header, 4 pins [form="♀ (female)"]
  C+3 = female pin header, 4 pins [form="♀ (female)"]
  D+4 = female pin header, 4 pins [form="♀ (female)"]
  D-4 = female pin header, 4 pins [form="♀ (female)"]
  Out+_3 = female pin header, 3 pins [form="♀ (female)"]
  Out-_3 = female pin header, 3 pins [form="♀ (female)"]
  D-5 = female pin header, 4 pins [form="♀ (female)"]
  D+5 = female pin header, 4 pins [form="♀ (female)"]
  Out+_4 = female pin header, 3 pins [form="♀ (female)"]
  Out-_4 = female pin header, 3 pins [form="♀ (female)"]

nets:
  N1: Out+.pin1, D-_2.pin1, D-_2.pin2
  N2: Out+.pin2, A+.pin7
  N3: Out+.pin3, Vin.pin2, D-_2.pin4, D+_2.pin4, C-_2.pin4, C+_2.pin4, B-_2.pin4, B+_2.pin4, B+1.pin4, B-1.pin4, C+1.pin4, C-1.pin4, D-1.pin4, Out-.pin3, D+1.pin4, C+2.pin4, C-2.pin4, D+2.pin4, D-2.pin4, Out+_2.pin3, Out-_2.pin3, D-3.pin4, D+3.pin4, C-3.pin4, C+3.pin4, D+4.pin4, D-4.pin4, Out+_3.pin3, Out-_3.pin3, D-5.pin4, D+5.pin4, Out+_4.pin3, Out-_4.pin3
  N4: A-.pin1, B+1.pin3
  N5: A-.pin2, B-1.pin3
  N6: A-.pin3, C+1.pin3
  N7: A-.pin4, C-1.pin3
  N8: A-.pin5, D+1.pin3
  N9: A-.pin6, D-1.pin3
  N10: A-.pin7, Out-.pin2
  N11: B+.pin1, C+2.pin3
  N12: B+.pin2, C-2.pin3
  N13: B+.pin3, D+2.pin3
  N14: B+.pin4, D-2.pin3
  N15: B+.pin5, Out+_2.pin2
  N16: B-.pin1, C+3.pin3
  N17: B-.pin2, C-3.pin3
  N18: B-.pin3, D+3.pin3
  N19: B-.pin4, D-3.pin3
  N20: B-.pin5, Out-_2.pin2
  N21: C+.pin1, D+4.pin3
  N22: C+.pin2, D-4.pin3
  N23: C+.pin3, Out+_3.pin2
  N24: C-.pin1, D+5.pin3
  N25: C-.pin2, D-5.pin3
  N26: C-.pin3, Out-_3.pin2
  N27: D+.pin1, Out+_4.pin2
  N28: D-.pin1, Out-_4.pin2
  N29: Vin.pin1, B+_2.pin1, B+_2.pin2, B+1.pin1, B+1.pin2, C+2.pin1, C+2.pin2, C+3.pin1, C+3.pin2, D+4.pin1, D+4.pin2, D+5.pin1, D+5.pin2, Out+_4.pin1, Out-_4.pin1
  N30: D-_2.pin3, A+.pin6
  N31: D+_2.pin1, D+_2.pin2, C-_2.pin1, C-_2.pin2
  N32: D+_2.pin3, A+.pin5
  N33: C-_2.pin3, A+.pin4
  N34: C+_2.pin1, C+_2.pin2, B-_2.pin1, B-_2.pin2
  N35: C+_2.pin3, A+.pin3
  N36: B-_2.pin3, A+.pin2
  N37: B+_2.pin3, A+.pin1
  N38: B-1.pin1, B-1.pin2, C+1.pin1, C+1.pin2
  N39: C-1.pin1, C-1.pin2, D+1.pin1, D+1.pin2
  N40: D-1.pin1, D-1.pin2, Out-.pin1
  N41: C-2.pin1, C-2.pin2, D+2.pin1, D+2.pin2
  N42: D-2.pin1, D-2.pin2, Out+_2.pin1
  N43: Out-_2.pin1, D-3.pin1, D-3.pin2
  N44: D+3.pin1, D+3.pin2, C-3.pin1, C-3.pin2
  N45: D-4.pin1, D-4.pin2, Out+_3.pin1
  N46: Out-_3.pin1, D-5.pin1, D-5.pin2

notes:
  V+
  B+
  B-
  C+
  C-
  D+
  D-
  Out+
  Out-
  GND
  A+
  A-
  12 jumpers
  Top
