# Fritzing sketch Overview MAX395 (saved by Fritzing 0.9.2b)
breadboards: 1

parts:
  I/O_Board = IC, DIP package, 26 pins [chip_label="I/O Board"]
  IVT-0 = IC, DIP package, 18 pins [chip_label=I/MVT]
  IC1 = IC, DIP package, 28 pins [chip_label="Switch Array"]
  IVT-1 = IC, DIP package, 18 pins [chip_label=I/MVT]
  IVT-2 = IC, DIP package, 18 pins [chip_label=I/MVT]
  IVT-3 = IC, DIP package, 18 pins [chip_label=I/MVT]
  Batt = DC Power [voltage=7.2 frequency=60]  # not connected
  Out-_Out+_D-_D+_C-_C+_B-_B+_A-_A+_GND = female pin header, 11 pins [form="♀ (female)"]
  MVT = IC, DIP package, 20 pins [chip_label=I/MVT]
  IC2 = IC, DIP package, 16 pins [chip_label="PSU & Pyboard"]

nets:
  N1: I/O_Board.pin1, Out-_Out+_D-_D+_C-_C+_B-_B+_A-_A+_GND.pin10
  N2: I/O_Board.pin2, Out-_Out+_D-_D+_C-_C+_B-_B+_A-_A+_GND.pin9
  N3: I/O_Board.pin3, Out-_Out+_D-_D+_C-_C+_B-_B+_A-_A+_GND.pin8
  N4: I/O_Board.pin4, Out-_Out+_D-_D+_C-_C+_B-_B+_A-_A+_GND.pin7
  N5: I/O_Board.pin5, Out-_Out+_D-_D+_C-_C+_B-_B+_A-_A+_GND.pin6
  N6: I/O_Board.pin6, Out-_Out+_D-_D+_C-_C+_B-_B+_A-_A+_GND.pin5
  N7: I/O_Board.pin7, Out-_Out+_D-_D+_C-_C+_B-_B+_A-_A+_GND.pin4
  N8: I/O_Board.pin8, Out-_Out+_D-_D+_C-_C+_B-_B+_A-_A+_GND.pin3
  N9: I/O_Board.pin9, Out-_Out+_D-_D+_C-_C+_B-_B+_A-_A+_GND.pin2
  N10: I/O_Board.pin10, Out-_Out+_D-_D+_C-_C+_B-_B+_A-_A+_GND.pin1
  N11: I/O_Board.pin11, IVT-0.pin1
  N12: I/O_Board.pin12, IVT-0.pin2
  N13: I/O_Board.pin13, IVT-0.pin3
  N14: I/O_Board.pin14, IVT-1.pin1
  N15: I/O_Board.pin15, IVT-1.pin2
  N16: I/O_Board.pin16, IVT-1.pin3
  N17: I/O_Board.pin17, IVT-2.pin1
  N18: I/O_Board.pin18, IVT-2.pin2
  N19: I/O_Board.pin19, IVT-2.pin3
  N20: I/O_Board.pin20, IVT-3.pin1
  N21: I/O_Board.pin21, IVT-3.pin2
  N22: I/O_Board.pin22, IVT-3.pin3
  N23: I/O_Board.pin23, MVT.pin4
  N24: I/O_Board.pin24, MVT.pin5
  N25: I/O_Board.pin25, MVT.pin6
  N26: I/O_Board.pin26, Out-_Out+_D-_D+_C-_C+_B-_B+_A-_A+_GND.pin11
  N27: IVT-0.pin4, IC1.pin1
  N28: IVT-0.pin5, IC1.pin2
  N29: IVT-0.pin6, IC1.pin3
  N30: IVT-0.pin7, IVT-1.pin13
  N31: IVT-0.pin8, IVT-1.pin14
  N32: IVT-0.pin9, IVT-1.pin15
  N33: IVT-0.pin10, IVT-1.pin16
  N34: IVT-0.pin11, IVT-1.pin17
  N35: IVT-0.pin12, IVT-1.pin18
  N36: IVT-0.pin13, IC1.pin22
  N37: IVT-0.pin14, IC1.pin23
  N38: IVT-0.pin15, IC1.pin24
  N39: IVT-0.pin16, IC1.pin19
  N40: IVT-0.pin17, IC1.pin20
  N41: IVT-0.pin18, IC1.pin21
  N42: IC1.pin4, IVT-1.pin4
  N43: IC1.pin5, IVT-1.pin5
  N44: IC1.pin6, IVT-1.pin6
  N45: IC1.pin7, IVT-2.pin4
  N46: IC1.pin8, IVT-2.pin5
  N47: IC1.pin9, IVT-2.pin6
  N48: IC1.pin10, IVT-3.pin4
  N49: IC1.pin11, IVT-3.pin5
  N50: IC1.pin12, IVT-3.pin6
  N51: IC1.pin13, MVT.pin1
  N52: IC1.pin14, MVT.pin2
  N53: IC1.pin15, MVT.pin3
  N54: IC1.pin16, IC2.pin9
  N55: IC1.pin17, IC2.pin10
  N56: IC1.pin18, IC2.pin11
  N57: IVT-1.pin7, IVT-2.pin13
  N58: IVT-1.pin8, IVT-2.pin14
  N59: IVT-1.pin9, IVT-2.pin15
  N60: IVT-1.pin10, IVT-2.pin16
  N61: IVT-1.pin11, IVT-2.pin17
  N62: IVT-1.pin12, IVT-2.pin18
  N63: IVT-2.pin7, IVT-3.pin13
  N64: IVT-2.pin8, IVT-3.pin14
  N65: IVT-2.pin9, IVT-3.pin15
  N66: IVT-2.pin10, IVT-3.pin16
  N67: IVT-2.pin11, IVT-3.pin17
  N68: IVT-2.pin12, IVT-3.pin18
  N69: IVT-3.pin7, MVT.pin14
  N70: IVT-3.pin8, MVT.pin15
  N71: IVT-3.pin9, MVT.pin16
  N72: IVT-3.pin10, MVT.pin17
  N73: IVT-3.pin11, MVT.pin18
  N74: IVT-3.pin12, MVT.pin19
  N75: MVT.pin7, IC2.pin1
  N76: MVT.pin8, IC2.pin2
  N77: MVT.pin9, IC2.pin3
  N78: MVT.pin10, IC2.pin12
  N79: MVT.pin11, IC2.pin13
  N80: MVT.pin12, IC2.pin14
  N81: MVT.pin13, IC2.pin15

notes:
  Guitar
