# Fritzing sketch ArduStomp02 (saved by Fritzing 0.7.12b)
breadboards: 3

parts:
  S1 = Pushbutton [package=THT]
  R1 = Resistor [tolerance=±5% resistance=10k package=THT]
  S2 = Pushbutton [package=THT]
  R2 = Resistor [tolerance=±5% resistance=10k package=THT]
  S3 = Pushbutton [package=THT]
  R3 = Resistor [tolerance=±5% resistance=10k package=THT]
  S4 = Pushbutton [package=THT]
  S5 = Pushbutton [package=THT]
  R5 = Resistor [tolerance=±5% resistance=10k package=THT]
  S6 = Pushbutton [package=THT]
  R6 = Resistor [tolerance=±5% resistance=10k package=THT]
  S7 = Pushbutton [package=THT]
  R7 = Resistor [tolerance=±5% resistance=10k package=THT]
  S8 = Pushbutton [package=THT]
  R8 = Resistor [tolerance=±5% resistance=10k package=THT]
  S9 = Pushbutton [package=THT]
  R9 = Resistor [tolerance=±5% resistance=10k package=THT]
  ARDUINO1 = Arduino Micro
  U1 = 74HC595 [package="DIP16 [THT]"]  # not connected
  U2 = 74HC595 [package="DIP16 [THT]"]  # not connected
  C1 = Electrolytic Capacitor [capacitance=1µF package="200 mil [THT, electrolytic]"]
  R15 = Resistor [tolerance=±5% resistance=1k package=THT]
  R16 = Resistor [tolerance=±5% resistance=1k package=THT]
  R17 = Resistor [tolerance=±5% resistance=1k package=THT]
  R18 = Resistor [tolerance=±5% resistance=1k package=THT]
  R19 = Resistor [tolerance=±5% resistance=1k package=THT]
  R20 = Resistor [tolerance=±5% resistance=1k package=THT]
  R21 = Resistor [tolerance=±5% resistance=1k package=THT]
  R26 = Resistor [tolerance=±5% resistance=1k package=THT]
  R27 = Resistor [tolerance=±5% resistance=1k package=THT]
  R28 = Resistor [tolerance=±5% resistance=1k package=THT]
  R29 = Resistor [tolerance=±5% resistance=1k package=THT]
  R30 = Resistor [tolerance=±5% resistance=10k package=THT]
  R31 = Resistor [tolerance=±5% resistance=1k package=THT]
  R32 = Resistor [tolerance=±5% resistance=1k package=THT]
  R33 = Resistor [tolerance=±5% resistance=1k package=THT]
  R34 = Resistor [tolerance=±5% resistance=1k package=THT]
  R35 = Resistor [tolerance=±5% resistance=1k package=THT]
  LED29 = Red LED - 5mm [package="5 mm [THT]"]
  LED30 = Red LED - 5mm [package="5 mm [THT]"]
  LED31 = Red LED - 5mm [package="5 mm [THT]"]
  LED33 = yellow LED - 5mm [package="5 mm [THT]"]
  LED32 = yellow LED - 5mm [package="5 mm [THT]"]
  LED35 = white LED - 5mm [package="5 mm [THT]"]
  LED39 = yellow LED - 5mm [package="5 mm [THT]"]
  LED41 = Red LED - 5mm [package="5 mm [THT]"]
  LED42 = Blue LED - 5mm [package="5 mm [THT]"]
  LED40 = green LED - 5mm [package="5 mm [THT]"]
  LED43 = green LED - 5mm [package="5 mm [THT]"]
  microSD1 = MicroSD Breakout
  Part1 = Bluetooth Mate Silver
  S10 = Pushbutton [package=THT]
  R36 = Resistor [tolerance=±5% resistance=10k package=THT]
  LED38 = green LED - 5mm [package="5 mm [THT]"]
  LED37 = green LED - 5mm [package="5 mm [THT]"]
  LED36 = green LED - 5mm [package="5 mm [THT]"]
  LED44 = Blue LED - 5mm [package="5 mm [THT]"]
  LED45 = Red LED - 5mm [package="5 mm [THT]"]

nets:
  N1: S1.Pin_1, S1.Pin_2, R1.Pin_1, ARDUINO1.D2
  5V: S1.Pin_3, S1.Pin_4, S2.Pin_3, S2.Pin_4, S3.Pin_3, S3.Pin_4, S4.Pin_3, S4.Pin_4, S5.Pin_3, S5.Pin_4, S6.Pin_3, S6.Pin_4, S7.Pin_3, S7.Pin_4, S8.Pin_3, S8.Pin_4, S9.Pin_3, S9.Pin_4, ARDUINO1.5V, microSD1.5V, Part1.VCC
  GND: R1.Pin_0, R2.Pin_0, R3.Pin_0, R5.Pin_0, R7.Pin_0, R8.Pin_0, R9.Pin_0, ARDUINO1.GND#31, R30.Pin_0, microSD1.GND, Part1.GND, R36.Pin_0
  N2: S2.Pin_1, S2.Pin_2, R2.Pin_1, ARDUINO1.D3
  N3: S3.Pin_1, S3.Pin_2, R3.Pin_1, ARDUINO1.D4
  N4: S4.Pin_1, S4.Pin_2, ARDUINO1.D5, R30.Pin_1
  N5: S5.Pin_1, S5.Pin_2, R5.Pin_1, ARDUINO1.D6
  N6: S6.Pin_1, S6.Pin_2, R6.Pin_1, ARDUINO1.D7
  N7: S7.Pin_1, S7.Pin_2, R7.Pin_1, ARDUINO1.D8
  N8: S8.Pin_1, S8.Pin_2, R8.Pin_1, ARDUINO1.D9
  N9: S9.Pin_1, S9.Pin_2, R9.Pin_1, ARDUINO1.D11
  N10: ARDUINO1.MOSI, microSD1.DI
  N11: ARDUINO1.TX, Part1.RX_5V
  N12: ARDUINO1.RX, Part1.TX_5V
  N13: ARDUINO1.D10, microSD1.CS
  N14: ARDUINO1.D12, S10.Pin_1, S10.Pin_2, R36.Pin_1
  N15: ARDUINO1.D13, C1.-
  N16: ARDUINO1.MISO, microSD1.DO
  N17: ARDUINO1.SCK, microSD1.CLK
  N18: R15.Pin_1, LED33.anode
  N19: R16.Pin_1, LED39.anode
  N20: R17.Pin_1, LED30.anode
  N21: R18.Pin_1, LED44.anode
  N22: R19.Pin_1, LED42.anode
  N23: R20.Pin_1, LED32.anode
  N24: R21.Pin_1, LED45.anode
  N25: R26.Pin_1, LED43.anode
  N26: R27.Pin_1, LED40.anode
  N27: R28.Pin_1, LED36.anode
  N28: R29.Pin_1, LED37.anode
  N29: R31.Pin_1, LED31.anode
  N30: R32.Pin_1, LED41.anode
  N31: R33.Pin_1, LED38.anode
  N32: R34.Pin_1, LED35.anode
  N33: R35.Pin_1, LED29.anode
  N34: LED29.cathode, LED30.cathode, LED31.cathode, LED33.cathode, LED32.cathode, LED35.cathode, LED39.cathode, LED41.cathode, LED38.cathode, LED37.cathode, LED36.cathode
  N35: LED42.cathode, LED40.cathode, LED43.cathode
  N36: S10.Pin_3, S10.Pin_4

notes:
  LEDs:
  MSB,
  Unsigned int :
  Byte 2: || Byte 1:
  7 6 5 4 3 2 1 0 || 7 6 0 1 3 2 5 4
  V V V T T T P P || P A N N M M B B
  2 1 0 2 1 0 2 1 || 0 0 1 0 1 0 1 0
  Buttons:
  V+ V- T+ T- N M B P A S
  ArduConf00::nbLeds[] =
  {2, // neck led
  2, // middle led
  2, // bridge leds 00 11 10 !!
  1, // auto led
  3, // 1st of the presets leds
  // end of first byte
  // 2 more presets leds
  3, // tone leds in binary !!!
  3} // vol leds in binary !!!
  ; // end of second byte!

custom parts:
  Arduino Micro: Arduino Micro Microcontroller
  MicroSD Breakout: 5V-ready microSD Breakout with Level Shifter
